# Fritzing sketch BuzzerFritzing (saved by Fritzing 0.9.3b)
breadboards: 1

parts:
  Part1 = Adafruit Trinket M0 [part_number="Adafruit #3500"]
  J1 = Piezo Speaker

nets:
  N1: Part1.GND, J1.pin1
  N2: Part1.D4_A2_PA06_TXD_MOSI, J1.pin2
